# Fritzing sketch Blink Scheme (saved by Fritzing 0.9.3b)
breadboards: 1

parts:
  U1 = NodeMCU V3.0
  LED1 = LED - 5mm [color="Red (633nm)" package="5 mm [THT]"]
  R1 = Resistor [tolerance=±10% resistance=330 package=THT]

nets:
  N1: U1.D0, LED1.anode
  N2: U1.RSV, R1.Pin_1
  N3: LED1.cathode, R1.Pin_0

custom parts:
  NodeMCU V3.0: NodeMcu V3 Lua WIFI Development Board
